// Digital circuit 16-bit-cpu.dig as structural Verilog
module _16_bit_cpu (
  output [15:0] R0,
  output [15:0] R1,
  output [15:0] R2,
  output [15:0] R3,
  output [3:0] PC
);

  wire clk, hex, instrdisplay_1_p1, instrdisplay_1_p2, instrdisplay_1_p3, instrdisplay_1_p4,
       instrdisplay_1_p5, instrdisplay_1_p6, jump, mem_org_1_c, mem_org_1_ld, mem_org_1_str, not_1_out,
       rd_display_1_p1, rd_display_1_p2, rs_display_1_p1, rs_display_1_p2, tworeg, val_display_1_p0,
       val_display_1_p1, val_display_1_p2, val_display_1_p3, val_display_1_p4, val_display_2_p0,
       val_display_2_p1, val_display_2_p2, val_display_2_p3, val_display_2_p4;
  wire [1:0] rd, rs;
  wire [2:0] op;
  wire [3:0] mem_org_1_a, val_display_1_d0, val_display_1_d1, val_display_1_d2, val_display_1_d3,
       val_display_1_d4, val_display_2_d0, val_display_2_d1, val_display_2_d2, val_display_2_d3,
       val_display_2_d4;
  wire [15:0] _32_to_16_splitter_1_p2, _32_to_16_splitter_1_p3, fetch_unit_1_inst_out, instrdisplay_1_d1,
       instrdisplay_1_d2, instrdisplay_1_d3, instrdisplay_1_d4, instrdisplay_1_d5, instrdisplay_1_d6, L,
       mem_org_1_din, Program_Mem_d, R, rd_display_1_d1, rd_display_1_d2, rs_display_1_d1, rs_display_1_d2,
       tst_adder_ic_1_res;

  Button advance (.out(clk));
  mem_org mem_org_1 (
    .PC(PC), .A(mem_org_1_a), .Din(mem_org_1_din), .str(mem_org_1_str), .C(mem_org_1_c), .ld(mem_org_1_ld));
  EEPROMDualPort #(.AddrBits(4), .isProgramMemory("true"), .Bits(16)) Program_Mem (
    .A(mem_org_1_a), .Din(mem_org_1_din), .str(mem_org_1_str), .C(mem_org_1_c), .ld(mem_org_1_ld),
    .D(Program_Mem_d));
  DipSwitch u_hex (.out(hex));
  fetch_unit fetch_unit_1 (
    .clock(clk), .address(R), .jump(jump), .inst_in(Program_Mem_d), .PC(PC), .Inst_out(fetch_unit_1_inst_out));
  SixteenSeg sixteenseg_1 (.led(rd_display_1_d1), .dp(rd_display_1_p1));
  SixteenSeg sixteenseg_2 (.led(rd_display_1_d2), .dp(rd_display_1_p2));
  rd_display rd_display_1 (
    .jmp(jump), .rd(rd), .D1(rd_display_1_d1), .P1(rd_display_1_p1), .D2(rd_display_1_d2),
    .P2(rd_display_1_p2));
  Seven_Seg_Hex seven_seg_hex_1 (.d(val_display_1_d4), .dp(val_display_1_p4));
  Seven_Seg_Hex seven_seg_hex_2 (.d(val_display_1_d3), .dp(val_display_1_p3));
  Seven_Seg_Hex seven_seg_hex_3 (.d(val_display_1_d2), .dp(val_display_1_p2));
  val_display val_display_1 (
    .inpt(L), .hex(hex), .en(not_1_out), .D4(val_display_1_d4), .P4(val_display_1_p4), .D3(val_display_1_d3),
    .P3(val_display_1_p3), .D2(val_display_1_d2), .P2(val_display_1_p2), .D1(val_display_1_d1),
    .P1(val_display_1_p1), .D0(val_display_1_d0), .P0(val_display_1_p0));
  not not_1 (not_1_out, jump);
  // _32_to_16_splitter _32_to_16_splitter_1: pin names not known; wires that end beside it: fetch_unit_1_inst_out, _32_to_16_splitter_1_p2, _32_to_16_splitter_1_p3, R, L, op, jump, rs, rd, tworeg
  Seven_Seg_Hex seven_seg_hex_4 (.d(val_display_1_d1), .dp(val_display_1_p1));
  Seven_Seg_Hex seven_seg_hex_5 (.d(val_display_1_d0), .dp(val_display_1_p0));
  SixteenSeg sixteenseg_3 (.led(instrdisplay_1_d1), .dp(instrdisplay_1_p1));
  SixteenSeg sixteenseg_4 (.led(instrdisplay_1_d2), .dp(instrdisplay_1_p2));
  SixteenSeg sixteenseg_5 (.led(instrdisplay_1_d3), .dp(instrdisplay_1_p3));
  instrdisplay instrdisplay_1 (
    .op(op), .D1(instrdisplay_1_d1), .P1(instrdisplay_1_p1), .D2(instrdisplay_1_d2), .P2(instrdisplay_1_p2),
    .D3(instrdisplay_1_d3), .P3(instrdisplay_1_p3), .D4(instrdisplay_1_d4), .P4(instrdisplay_1_p4),
    .D5(instrdisplay_1_d5), .P5(instrdisplay_1_p5), .D6(instrdisplay_1_d6), .P6(instrdisplay_1_p6));
  SixteenSeg sixteenseg_6 (.led(instrdisplay_1_d4), .dp(instrdisplay_1_p4));
  SixteenSeg sixteenseg_7 (.led(instrdisplay_1_d5), .dp(instrdisplay_1_p5));
  Tst_adder_ic tst_adder_ic_1 (.R(R), .L(L), .op(op), .Res(tst_adder_ic_1_res));
  SixteenSeg sixteenseg_8 (.led(instrdisplay_1_d6), .dp(instrdisplay_1_p6));
  Seven_Seg_Hex seven_seg_hex_6 (.d(val_display_2_d4), .dp(val_display_2_p4));
  Seven_Seg_Hex seven_seg_hex_7 (.d(val_display_2_d3), .dp(val_display_2_p3));
  Seven_Seg_Hex seven_seg_hex_8 (.d(val_display_2_d2), .dp(val_display_2_p2));
  val_display val_display_2 (
    .inpt(R), .hex(hex), .en(1'b1), .D4(val_display_2_d4), .P4(val_display_2_p4), .D3(val_display_2_d3),
    .P3(val_display_2_p3), .D2(val_display_2_d2), .P2(val_display_2_p2), .D1(val_display_2_d1),
    .P1(val_display_2_p1), .D0(val_display_2_d0), .P0(val_display_2_p0));
  register_file register_file_1 (
    .rs(rs), .rd(rd), .res(tst_adder_ic_1_res), .clk(clk), .R0(R0), .R1(R1), .R2(R2), .R3(R3),
    .rsval(_32_to_16_splitter_1_p2), .rdval(_32_to_16_splitter_1_p3));
  Seven_Seg_Hex seven_seg_hex_9 (.d(val_display_2_d1), .dp(val_display_2_p1));
  Seven_Seg_Hex seven_seg_hex_10 (.d(val_display_2_d0), .dp(val_display_2_p0));
  SixteenSeg sixteenseg_9 (.led(rs_display_1_d1), .dp(rs_display_1_p1));
  SixteenSeg sixteenseg_10 (.led(rs_display_1_d2), .dp(rs_display_1_p2));
  rs_display rs_display_1 (
    .rs(rs), .jmp(jump), .tworeg(tworeg), .D1(rs_display_1_d1), .P1(rs_display_1_p1), .D2(rs_display_1_d2),
    .P2(rs_display_1_p2));

  // Notes on the sheet:
  //   0: R2 = R2 + 1
  //   1: R2 = R2 + R1
  //   2: R3 = R2 
  //   3: R1 = R1 + R2
  //   4: R3 = R1
  //   5: jump 1
  //   contents of Program_Mem (hex, n*v repeats v):
  //   120,61,bd,91,7d,10e
endmodule
