// Digital circuit 32_to_16_splitter.dig as structural Verilog
module _32_to_16_splitter (
  input  [15:0] rdval,
  input  [15:0] Din,
  input  [15:0] rsval,
  output [15:0] R,
  output [15:0] L,
  output [4:0] op,
  output jmp,
  output [1:0] rs,
  output [1:0] rd,
  output tworeg
);

  wire imm5_valid, imm11_valid, rd_valid, rs_valid, sys;
  wire [3:2] multiplexer_1_out, multiplexer_2_out;
  wire [4:0] op_raw;
  wire [4:4] nop;
  wire [15:0] imm5, imm11, multiplexer_3_out, multiplexer_4_out;

  BitExtender #(.inputBits(5)) bitextender_1 (.in(Din[15:11]), .out(imm5));
  BitExtender #(.inputBits(11)) bitextender_2 (.in(Din[15:5]), .out(imm11));
  instdecoder instdecoder_1 (
    .fmt(Din[2:0]), .op1(Din[4:3]), .op2(Din[10:7]), .op3(Din[15:11]), .op(op_raw), .tworeg(tworeg),
    .sys(sys), .imm11_valid(imm11_valid), .imm5_valid(imm5_valid), .rs_valid(rs_valid), .rd_valid(rd_valid));
  Multiplexer #(.Bits(4)) multiplexer_1 (
    .sel(rs_valid), .in_0(4'b0000), .in_1(Din[10:7]), .out({multiplexer_1_out, rs}));
  Multiplexer #(.Bits(4)) multiplexer_2 (
    .sel(rd_valid), .in_0(4'b0000), .in_1(Din[6:3]), .out({multiplexer_2_out, rd}));
  Multiplexer #(.Bits(16)) multiplexer_3 (.sel(imm11_valid), .in_0(imm5), .in_1(imm11), .out(multiplexer_3_out));
  Multiplexer #(.Bits(16)) multiplexer_4 (.sel(rs_valid), .in_0({16{1'b0}}), .in_1(rsval), .out(multiplexer_4_out));
  Multiplexer #(.Bits(5)) multiplexer_5 (.sel(sys), .in_0(op_raw), .in_1({nop[4], 4'b1000}), .out(op));
  Multiplexer #(.Bits(16)) multiplexer_6 (.sel(tworeg), .in_0(multiplexer_3_out), .in_1(multiplexer_4_out), .out(R));
  Multiplexer #(.Bits(16)) multiplexer_7 (.sel(rd_valid), .in_0({16{1'b0}}), .in_1(rdval), .out(L));
  and and_1 (jmp, op[2], ~op[3], ~op[4]);  // And
  // Pins of 4 and 5 bits meet at {nop[4], 4'b1000}

  // Other names for the same wires on the sheet: rd_t[3:0] = Din[6:3]; rs_t[3:0] = Din[10:7]
endmodule
