// Digital circuit Asm.dig as structural Verilog
module Asm (
  input  prog,
  input  [7:0] imm,
  input  [1:0] dest,
  input  [1:0] src,
  input  add,
  input  jump,
  input  two_reg,
  input  move,
  output store_clk,
  output [15:0] inst
);

  wire priorityencoder_1_any;

  PriorityEncoder #(.Selector_Bits(3)) priorityencoder_1 (
    .in0(add), .in1(1'b0), .in2(1'b0), .in3(1'b0), .in4(1'b0), .in5(1'b0), .in6(move), .in7(jump),
    .num(inst[3:1]), .any(priorityencoder_1_any));
  and and_1 (store_clk, priorityencoder_1_any, prog);

  assign {inst[15:4], inst[0]} = {imm, src, dest, two_reg};

  // Notes on the sheet:
  //   imm: default 18
  //   add: default 200
  //   jump: default 200
endmodule
