// Digital circuit Tst_adder_ic.dig as structural Verilog
module Tst_adder_ic (
  input  [15:0] R,
  input  [15:0] L,
  input  [2:0] op,
  output [15:0] Res
);

  wire [15:0] add_1_s;

  Add #(.Bits(16)) add_1 (.a(R), .b(L), .c_i(1'b0), .s(add_1_s));  // open: c_o
  Multiplexer #(.Selector_Bits(3), .Bits(16)) multiplexer_1 (
    .sel(op), .in_0(add_1_s), .in_1({16{1'b0}}), .in_2({16{1'b0}}), .in_3({16{1'b0}}), .in_4({16{1'b0}}),
    .in_5({16{1'b0}}), .in_6(R), .in_7(L), .out(Res));
endmodule
