// Digital circuit binary_to_decimal.dig as structural Verilog
module binary_to_decimal (
  input  [15:0] inpt,
  output [3:0] D4,
  output [3:0] D3,
  output [3:0] D2,
  output [3:0] D1,
  output [3:0] D0
);

  wire [15:0] div_1_q, div_2_q, div_3_q, div_4_q;
  wire [15:4] div_1_r, div_2_r, div_3_r, div_4_r, div_5_r;

  Div #(.Bits(16)) div_1 (.a(inpt), .b(16'ha), .q(div_1_q), .r({div_1_r, D0}));
  Div #(.Bits(16)) div_2 (.a(div_1_q), .b(16'ha), .q(div_2_q), .r({div_2_r, D1}));
  Div #(.Bits(16)) div_3 (.a(div_2_q), .b(16'ha), .q(div_3_q), .r({div_3_r, D2}));
  Div #(.Bits(16)) div_4 (.a(div_3_q), .b(16'ha), .q(div_4_q), .r({div_4_r, D3}));
  Div #(.Bits(16)) div_5 (.a(div_4_q), .b(16'ha), .r({div_5_r, D4}));  // open: q
endmodule
