// Digital circuit register_file.dig as structural Verilog
module register_file (
  input  [1:0] rs,
  input  [1:0] rd,
  input  [15:0] res,
  input  clk,
  output [15:0] R0,
  output [15:0] R1,
  output [15:0] R2,
  output [15:0] R3,
  output [15:0] rsval,
  output [15:0] rdval
);

  wire demultiplexer_2_out_0, demultiplexer_2_out_1, demultiplexer_2_out_2, demultiplexer_2_out_3;
  wire [15:0] demultiplexer_1_out_0, demultiplexer_1_out_1, demultiplexer_1_out_2, demultiplexer_1_out_3;

  Demultiplexer #(.Selector_Bits(2), .Bits(16)) demultiplexer_1 (
    .sel(rd), .in(res), .out_0(demultiplexer_1_out_0), .out_1(demultiplexer_1_out_1),
    .out_2(demultiplexer_1_out_2), .out_3(demultiplexer_1_out_3));
  Demultiplexer #(.Selector_Bits(2)) demultiplexer_2 (
    .sel(rd), .in(1'b1), .out_0(demultiplexer_2_out_0), .out_1(demultiplexer_2_out_1),
    .out_2(demultiplexer_2_out_2), .out_3(demultiplexer_2_out_3));
  Register #(.Bits(16)) u_R0 (.D(demultiplexer_1_out_0), .C(clk), .en(demultiplexer_2_out_0), .Q(R0));
  Register #(.Bits(16)) u_R1 (.D(demultiplexer_1_out_1), .C(clk), .en(demultiplexer_2_out_1), .Q(R1));
  Register #(.Bits(16)) u_R2 (.D(demultiplexer_1_out_2), .C(clk), .en(demultiplexer_2_out_2), .Q(R2));
  Register #(.Bits(16)) u_R3 (.D(demultiplexer_1_out_3), .C(clk), .en(demultiplexer_2_out_3), .Q(R3));
  Multiplexer #(.Selector_Bits(2), .Bits(16)) multiplexer_1 (
    .sel(rs), .in_0(R0), .in_1(R1), .in_2(R2), .in_3(R3), .out(rsval));
  Multiplexer #(.Selector_Bits(2), .Bits(16)) multiplexer_2 (
    .sel(rd), .in_0(R0), .in_1(R1), .in_2(R2), .in_3(R3), .out(rdval));
endmodule
