// Digital circuit val_display.dig as structural Verilog
module val_display (
  input  [15:0] inpt,
  input  hex,
  input  en,
  output [3:0] D4,
  output P4,
  output [3:0] D3,
  output P3,
  output [3:0] D2,
  output P2,
  output [3:0] D1,
  output P1,
  output [3:0] D0,
  output P0
);

  wire or_1_out, or_2_out, or_3_out, or_4_out;
  wire [3:0] binary_to_decimal_1_d0, binary_to_decimal_1_d1, binary_to_decimal_1_d2, binary_to_decimal_1_d3,
       binary_to_decimal_1_d4, multiplexer_1_out, multiplexer_2_out, multiplexer_3_out, multiplexer_4_out,
       multiplexer_5_out, multiplexer_6_out, multiplexer_7_out, multiplexer_8_out, multiplexer_9_out;

  binary_to_decimal binary_to_decimal_1 (
    .inpt(inpt), .D4(binary_to_decimal_1_d4), .D3(binary_to_decimal_1_d3), .D2(binary_to_decimal_1_d2),
    .D1(binary_to_decimal_1_d1), .D0(binary_to_decimal_1_d0));
  or or_1 (or_1_out, multiplexer_2_out[0], multiplexer_2_out[1], multiplexer_2_out[2], multiplexer_2_out[3]);
  Multiplexer #(.Bits(4)) multiplexer_1 (
    .sel(hex), .in_0(binary_to_decimal_1_d4), .in_1(4'b0000), .out(multiplexer_1_out));
  Multiplexer #(.Bits(4)) multiplexer_2 (.sel(en), .in_0(4'b0000), .in_1(multiplexer_1_out), .out(multiplexer_2_out));
  assign D4 = or_1_out ? multiplexer_2_out : 4'bz;  // Driver driver_1
  Multiplexer #(.Bits(4)) multiplexer_3 (.sel(en), .in_0(4'b0000), .in_1(multiplexer_4_out), .out(multiplexer_3_out));
  Multiplexer #(.Bits(4)) multiplexer_4 (
    .sel(hex), .in_0(binary_to_decimal_1_d3), .in_1(inpt[15:12]), .out(multiplexer_4_out));
  or or_2 (or_2_out, multiplexer_3_out[0], multiplexer_3_out[1], multiplexer_3_out[2], multiplexer_3_out[3], or_1_out);
  assign D3 = or_2_out ? multiplexer_3_out : 4'bz;  // Driver driver_2
  Multiplexer #(.Bits(4)) multiplexer_5 (.sel(en), .in_0(4'b0000), .in_1(multiplexer_6_out), .out(multiplexer_5_out));
  Multiplexer #(.Bits(4)) multiplexer_6 (
    .sel(hex), .in_0(binary_to_decimal_1_d2), .in_1(inpt[11:8]), .out(multiplexer_6_out));
  or or_3 (or_3_out, multiplexer_5_out[0], multiplexer_5_out[1], multiplexer_5_out[2], multiplexer_5_out[3], or_2_out);
  assign D2 = or_3_out ? multiplexer_5_out : 4'bz;  // Driver driver_3
  Multiplexer #(.Bits(4)) multiplexer_7 (.sel(en), .in_0(4'b0000), .in_1(multiplexer_8_out), .out(multiplexer_7_out));
  Multiplexer #(.Bits(4)) multiplexer_8 (
    .sel(hex), .in_0(binary_to_decimal_1_d1), .in_1(inpt[7:4]), .out(multiplexer_8_out));
  or or_4 (or_4_out, multiplexer_7_out[0], multiplexer_7_out[1], multiplexer_7_out[2], multiplexer_7_out[3], or_3_out);
  assign D1 = or_4_out ? multiplexer_7_out : 4'bz;  // Driver driver_4
  Multiplexer #(.Bits(4)) multiplexer_9 (
    .sel(hex), .in_0(binary_to_decimal_1_d0), .in_1(inpt[3:0]), .out(multiplexer_9_out));
  assign D0 = en ? multiplexer_9_out : 4'bz;  // Driver driver_5

  assign P0 = 1'b0;
  assign P1 = 1'b0;
  assign P2 = 1'b0;
  assign P3 = 1'b0;
  assign P4 = 1'b0;
endmodule
