// Digital circuit fetch unit.dig as structural Verilog
module fetch_unit (
  input  clock,
  input  [15:0] address,
  input  jump,
  input  [15:0] inst_in,
  output [3:0] PC,
  output [15:0] Inst_out
);

  CounterPreset #(.Bits(4)) counterpreset_1 (
    .en(1'b1), .C(clock), .dir(1'b0), .in(address[3:0]), .ld(jump), .clr(1'b0), .out(PC));  // open: ovf

  assign Inst_out = inst_in;
endmodule
