// Digital circuit instdecoder.dig as structural Verilog
module instdecoder (
  input  [2:0] fmt,
  input  [1:0] op1,
  input  [3:0] op2,
  input  [4:0] op3,
  output [4:0] op,
  output tworeg,
  output sys,
  output imm11_valid,
  output imm5_valid,
  output rs_valid,
  output rd_valid
);

  wire and_1_out, and_2_out;

  and and_1 (and_1_out, fmt[0], fmt[1]);
  and and_2 (and_2_out, ~fmt[0], fmt[1]);  // And
  and and_3 (imm11_valid, ~fmt[1], ~fmt[2]);  // And
  or or_1 (imm5_valid, and_1_out, fmt[2]);
  not not_1 (rd_valid, imm5_valid);
  or or_2 (rs_valid, and_2_out, fmt[2]);
  Multiplexer #(.Selector_Bits(3), .Bits(5)) multiplexer_1 (
    .sel(fmt), .in_0({3'b000, op1}), .in_1({3'b001, op1}), .in_2(op3), .in_3({1'b1, op2}),
    .in_4({3'b000, fmt[1:0]}), .in_5({3'b000, fmt[1:0]}), .in_6({3'b000, fmt[1:0]}),
    .in_7({3'b000, fmt[1:0]}), .out(op));
  and and_4 (tworeg, ~fmt[0], fmt[1], ~fmt[2]);  // And
  and and_5 (sys, ~fmt[0], ~fmt[1], ~fmt[2]);  // And

  // Other names for the same wires on the sheet: op0[1:0] = fmt[1:0]
endmodule
