// Digital circuit rd_display.dig as structural Verilog
module rd_display (
  input  jmp,
  input  [1:0] rd,
  output [15:0] D1,
  output P1,
  output [15:0] D2,
  output P2
);

  wire [6:0] multiplexer_1_out, multiplexer_2_out, multiplexer_3_out;

  Multiplexer #(.Bits(7)) multiplexer_1 (.sel(jmp), .in_0(7'b1010010), .in_1(7'b1010000), .out(multiplexer_1_out));
  ROM #(.AddrBits(7), .Bits(16)) ASCII (.A(multiplexer_1_out), .sel(1'b1), .D(D1));
  Multiplexer #(.Selector_Bits(2), .Bits(7)) multiplexer_2 (
    .sel(rd), .in_0(7'b0110000), .in_1(7'b0110001), .in_2(7'b0110010), .in_3(7'b0110011),
    .out(multiplexer_2_out));
  Multiplexer #(.Bits(7)) multiplexer_3 (
    .sel(jmp), .in_0(multiplexer_2_out), .in_1(7'b1000011), .out(multiplexer_3_out));
  ROM #(.AddrBits(7), .Bits(16)) ASCII_2 (.A(multiplexer_3_out), .sel(1'b1), .D(D2));

  assign P1 = 1'b0;
  assign P2 = 1'b0;

  // Notes on the sheet:
  //   contents of ASCII (hex, n*v repeats v):
  //   90ff,c,377,33f,38c,3bb,3fb,f,3ff,3bf,3cf,4a3f,f3,483f,3f3,1c3
  //   ,32*0,90ff,c,377,33f,38c,3bb,3fb,f,3ff,3bf,7*0,3cf,4a3f,f3,483f
  //   ,3f3,1c3,2fb,3cc,4833,7c,31c0,f0,14cc,24cc,ff,3c7,20ff,23c7,3bb
  //   ,4803,fc,90c0,a0cc,b400,5400,9033
  //   contents of ASCII_2 (hex, n*v repeats v):
  //   90ff,c,377,33f,38c,3bb,3fb,f,3ff,3bf,3cf,4a3f,f3,483f,3f3,1c3
  //   ,32*0,90ff,c,377,33f,38c,3bb,3fb,f,3ff,3bf,7*0,3cf,4a3f,f3,483f
  //   ,3f3,1c3,2fb,3cc,4833,7c,31c0,f0,14cc,24cc,ff,3c7,20ff,23c7,3bb
  //   ,4803,fc,90c0,a0cc,b400,5400,9033
endmodule
